// Logisim project P0_L0_CRC.circ as structural Verilog: 4 circuits, main circuit CRC
module CRC (
  input  [7:0] in_1,
  input  [3:0] in_2,
  output [10:0] out_3
);

  mod_2_divisor mod_2_divisor_1 (.dividend(in_1), .divisor(in_2), .out_3(out_3));
endmodule

module mod_2_divisor (
  input  [7:0] dividend,
  input  [3:0] divisor,
  output [10:0] out_3
);

  wire first_divisor_1_result, n4bit_mod2_half_divisor_1_result, n4bit_mod2_half_divisor_2_result,
       n4bit_mod2_half_divisor_3_result, n4bit_mod2_half_divisor_4_result, n4bit_mod2_half_divisor_5_result,
       n4bit_mod2_half_divisor_6_result, n4bit_mod2_half_divisor_7_result;
  wire [2:0] first_divisor_1_remainer, n4bit_mod2_half_divisor_1_remainer,
       n4bit_mod2_half_divisor_2_remainer, n4bit_mod2_half_divisor_3_remainer,
       n4bit_mod2_half_divisor_4_remainer, n4bit_mod2_half_divisor_5_remainer,
       n4bit_mod2_half_divisor_6_remainer;

  first_divisor first_divisor_1 (
    .dividend(dividend[7:4]), .divisor(divisor), .remainer(first_divisor_1_remainer),
    .result(first_divisor_1_result));
  _4bit_mod2_half_divisor u_4bit_mod2_half_divisor_1 (
    .remainer(n4bit_mod2_half_divisor_1_remainer), .divisor(divisor),
    .result(n4bit_mod2_half_divisor_1_result), .dividend(first_divisor_1_remainer), .next_bit(dividend[3]));
  _4bit_mod2_half_divisor u_4bit_mod2_half_divisor_2 (
    .remainer(n4bit_mod2_half_divisor_2_remainer), .divisor(divisor),
    .result(n4bit_mod2_half_divisor_2_result), .dividend(n4bit_mod2_half_divisor_1_remainer),
    .next_bit(dividend[2]));
  _4bit_mod2_half_divisor u_4bit_mod2_half_divisor_3 (
    .remainer(n4bit_mod2_half_divisor_3_remainer), .divisor(divisor),
    .result(n4bit_mod2_half_divisor_3_result), .dividend(n4bit_mod2_half_divisor_2_remainer),
    .next_bit(dividend[1]));
  _4bit_mod2_half_divisor u_4bit_mod2_half_divisor_4 (
    .remainer(n4bit_mod2_half_divisor_4_remainer), .divisor(divisor),
    .result(n4bit_mod2_half_divisor_4_result), .dividend(n4bit_mod2_half_divisor_3_remainer),
    .next_bit(dividend[0]));
  _4bit_mod2_half_divisor u_4bit_mod2_half_divisor_5 (
    .remainer(n4bit_mod2_half_divisor_5_remainer), .divisor(divisor),
    .result(n4bit_mod2_half_divisor_5_result), .dividend(n4bit_mod2_half_divisor_4_remainer), .next_bit(1'b0));
  _4bit_mod2_half_divisor u_4bit_mod2_half_divisor_6 (
    .remainer(n4bit_mod2_half_divisor_6_remainer), .divisor(divisor),
    .result(n4bit_mod2_half_divisor_6_result), .dividend(n4bit_mod2_half_divisor_5_remainer), .next_bit(1'b0));
  _4bit_mod2_half_divisor u_4bit_mod2_half_divisor_7 (
    .remainer(out_3[2:0]), .divisor(divisor), .result(n4bit_mod2_half_divisor_7_result),
    .dividend(n4bit_mod2_half_divisor_6_remainer), .next_bit(1'b0));
  // Probe on 1'b0
  // Probe on 1'b0
  // Probe on 1'b0
  // Probe on dividend[0]
  // Probe on dividend[1]
  // Probe on dividend[2]
  // Probe on dividend[3]
  // Probe on dividend[7:4]

  assign out_3[10:3] = dividend;

  // Other names for the same wires on the sheet: _7 = dividend[0]; _6 = dividend[1]; _5 = dividend[2];
  //   _4 = dividend[3]; first[3:0] = dividend[7:4]
endmodule

module _4bit_mod2_half_divisor (
  input  next_bit,
  input  [2:0] dividend,
  input  [3:0] divisor,
  output [2:0] remainer,
  output result
);

  wire [3:0] multiplexer_1_out, xor_1_out;

  BitSelector #(.width(4)) bitselector_1 (.in({dividend, next_bit}), .out(result), .sel(2'b11));
  Multiplexer #(.width(4)) multiplexer_1 (
    .in0(4'b0000), .in1(divisor), .out(multiplexer_1_out), .sel(result));  // open: en
  // Probe on {dividend, next_bit}
  // Probe on result
  BitSelector #(.width(4), .group(3)) bitselector_2 (.in(xor_1_out), .out(remainer), .sel(1'b0));
  assign xor_1_out = {dividend, next_bit} ^ multiplexer_1_out;  // XOR_Gate xor_1, 4 bits wide

  // Other names for the same wires on the sheet: dividend_t[3:0] = {dividend, next_bit}; highest = result
endmodule

module first_divisor (
  input  [3:0] dividend,
  input  [3:0] divisor,
  output [2:0] remainer,
  output result
);

  wire [3:0] multiplexer_1_out, xor_1_out;

  BitSelector #(.width(4)) bitselector_1 (.in(dividend), .out(result), .sel(2'b11));
  Multiplexer #(.width(4)) multiplexer_1 (
    .in0(4'b0000), .in1(divisor), .out(multiplexer_1_out), .sel(result));  // open: en
  assign xor_1_out = dividend ^ multiplexer_1_out;  // XOR_Gate xor_1, 4 bits wide
  BitSelector #(.width(4), .group(3)) bitselector_2 (.in(xor_1_out), .out(remainer), .sel(1'b0));

  // Other names for the same wires on the sheet: highest = result
endmodule
