// Logisim project P0_L0_FSM.circ as structural Verilog
module fsm (
  input  CLR,
  input  [1:0] In,
  output Z
);

  wire clock_1_out;
  wire [2:0] \状态储存_state , \状态转移_next_state ;

  // Probe on \状态转移_next_state 
  state_trans \u_状态转移  (.state(\状态储存_state ), .\input (In), .reset(CLR), .next_state(\状态转移_next_state ));
  Clock clock_1 (.out(clock_1_out));
  // Probe on \状态储存_state 
  state_store \u_状态储存  (.next_state(\状态转移_next_state ), .clk(clock_1_out), .reset(1'b0), .state(\状态储存_state ));
  \output  \u_输出  (.in_1(In), .state(\状态储存_state ), .out(Z));

  // Other names for the same wires on the sheet: reset = CLR

  // Notes on the sheet:
  //   baa
  //   bcc
  //   bbaa
  //   bbcc
  //   bac
  //   bca
  //   bbac
  //   bbca
endmodule

module state_trans (
  input  [2:0] state,
  input  [1:0] \input ,
  input  reset,
  output [2:0] next_state
);

  wire _0, _1, _2, _3, _4, a, and_1_out, and_2_out, b, c, d, not_1_out, not_2_out, or_1_out, or_3_out,
       or_4_out, or_5_out, or_6_out, to0, to1, to2, to3, to4;
  wire [2:0] bitfinder_1_index;

  not not_1 (not_1_out, b);
  not not_2 (not_2_out, b);
  or or_1 (or_1_out, _3, _0, _4);
  and and_1 (and_1_out, _0, not_1_out);
  and and_2 (and_2_out, _4, not_2_out);
  and and_3 (to1, or_1_out, b);
  Decoder #(.select(2)) decoder_1 (.out0(a), .out1(b), .out2(c), .out3(d), .sel(\input ));  // open: en
  or or_2 (to0, and_1_out, d, and_2_out);
  or or_3 (or_3_out, _1, _2);
  or or_4 (or_4_out, _1, _2);
  or or_5 (or_5_out, a, c);
  or or_6 (or_6_out, a, c);
  Decoder #(.select(3)) decoder_2 (
    .out0(_0), .out1(_1), .out2(_2), .out3(_3), .out4(_4), .sel(state));  // open: out5, out6, out7, en
  and and_4 (to2, or_3_out, b);
  and and_5 (to3, or_4_out, or_5_out);
  and and_6 (to4, _3, or_6_out);
  // Probe on bitfinder_1_index
  BitFinder #(.width(5)) bitfinder_1 (.in({to4, to3, to2, to1, to0}), .index(bitfinder_1_index));  // open: found
  Multiplexer #(.width(3)) multiplexer_1 (
    .in0(bitfinder_1_index), .in1(3'b000), .out(next_state), .sel(reset));  // open: en
endmodule

module state_store (
  input  [2:0] next_state,
  input  clk,
  input  reset,
  output [2:0] state
);

  Register #(.width(3)) register_1 (.D(next_state), .Q(state), .clk(clk), .clr(reset));  // open: en

  // Notes on the sheet:
  //   00 for nothing
  //   01 for 1 'b' detected
  //   02 for 2 'b' detected
  //   03 for 1 'a'/'c' detected
  //   04 for 2 'a'/'c' detected
endmodule

module \output  (
  input  [1:0] in_1,
  input  [2:0] state,
  output out
);

  wire comparator_1_eq, comparator_2_eq, comparator_3_eq, or_1_out;

  Comparator #(.width(2)) comparator_1 (.a(2'b00), .b(in_1), .eq(comparator_1_eq));  // open: gt, lt
  Comparator #(.width(2)) comparator_2 (.a(in_1), .b(2'b10), .eq(comparator_2_eq));  // open: gt, lt
  or or_1 (or_1_out, comparator_1_eq, comparator_2_eq);
  Comparator #(.width(3)) comparator_3 (.a(state), .b(3'b011), .eq(comparator_3_eq));  // open: gt, lt
  and and_1 (out, or_1_out, comparator_3_eq);
endmodule
