// Logisim project P0_L0_GRF.circ as structural Verilog: 1 circuit, main circuit grf
module grf (
  input  clk,
  input  reset,
  input  WE,
  input  [4:0] A1,
  input  [4:0] A2,
  input  [4:0] A3,
  input  [31:0] WD,
  output [31:0] RD1,
  output [31:0] RD2
);

  wire w0, w1, w2, w3, w4, w5, w6, w7, w8, w9, w10, w11, w12, w13, w14, w15, w16, w17, w18, w19, w20, w21,
       w22, w23, w24, w25, w26, w27, w28, w29, w30, w31, we_t;
  wire [31:0] multiplexer_1_out, multiplexer_2_out, multiplexer_3_out, multiplexer_4_out, multiplexer_5_out,
       multiplexer_6_out, multiplexer_7_out, multiplexer_8_out, multiplexer_9_out, multiplexer_10_out,
       multiplexer_11_out, multiplexer_12_out, multiplexer_13_out, multiplexer_14_out, multiplexer_15_out,
       multiplexer_16_out, multiplexer_17_out, multiplexer_18_out, multiplexer_19_out, multiplexer_20_out,
       multiplexer_21_out, multiplexer_22_out, multiplexer_23_out, multiplexer_25_out, multiplexer_26_out,
       multiplexer_27_out, multiplexer_28_out, multiplexer_29_out, multiplexer_30_out, multiplexer_31_out,
       multiplexer_32_out, reg0, reg1, reg2, reg3, reg4, reg5, reg6, reg7, reg8, reg9, reg10, reg11, reg12,
       reg13, reg14, reg15, reg16, reg17, reg18, reg19, reg20, reg21, reg22, reg23, reg24, reg25, reg26,
       reg27, reg28, reg29, reg30, reg31;

  Register #(.width(32)) register_1 (.Q(reg0), .clk(we_t), .clr(reset));  // open: D, en
  Register #(.width(32)) register_2 (.D(multiplexer_1_out), .Q(reg1), .clk(we_t), .clr(reset));  // open: en
  Multiplexer #(.width(32)) multiplexer_1 (.in0(reg1), .in1(WD), .out(multiplexer_1_out), .sel(w1));  // open: en
  Multiplexer #(.width(32)) multiplexer_2 (.in0(reg2), .in1(WD), .out(multiplexer_2_out), .sel(w2));  // open: en
  Register #(.width(32)) register_3 (.D(multiplexer_2_out), .Q(reg2), .clk(we_t), .clr(reset));  // open: en
  Register #(.width(32)) register_4 (.D(multiplexer_3_out), .Q(reg3), .clk(we_t), .clr(reset));  // open: en
  Multiplexer #(.width(32)) multiplexer_3 (.in0(reg3), .in1(WD), .out(multiplexer_3_out), .sel(w3));  // open: en
  Register #(.width(32)) register_5 (.D(multiplexer_4_out), .Q(reg4), .clk(we_t), .clr(reset));  // open: en
  Multiplexer #(.width(32)) multiplexer_4 (.in0(reg4), .in1(WD), .out(multiplexer_4_out), .sel(w4));  // open: en
  Multiplexer #(.width(32)) multiplexer_5 (.in0(reg5), .in1(WD), .out(multiplexer_5_out), .sel(w5));  // open: en
  Register #(.width(32)) register_6 (.D(multiplexer_5_out), .Q(reg5), .clk(we_t), .clr(reset));  // open: en
  Register #(.width(32)) register_7 (.D(multiplexer_6_out), .Q(reg6), .clk(we_t), .clr(reset));  // open: en
  Multiplexer #(.width(32)) multiplexer_6 (.in0(reg6), .in1(WD), .out(multiplexer_6_out), .sel(w6));  // open: en
  Multiplexer #(.width(32)) multiplexer_7 (.in0(reg7), .in1(WD), .out(multiplexer_7_out), .sel(w7));  // open: en
  Register #(.width(32)) register_8 (.D(multiplexer_7_out), .Q(reg7), .clk(we_t), .clr(reset));  // open: en
  and and_1 (we_t, clk, WE);
  Decoder #(.select(5)) decoder_1 (
    .out0(w0), .out1(w1), .out2(w2), .out3(w3), .out4(w4), .out5(w5), .out6(w6), .out7(w7), .out8(w8),
    .out9(w9), .out10(w10), .out11(w11), .out12(w12), .out13(w13), .out14(w14), .out15(w15), .out16(w16),
    .out17(w17), .out18(w18), .out19(w19), .out20(w20), .out21(w21), .out22(w22), .out23(w23), .out24(w24),
    .out25(w25), .out26(w26), .out27(w27), .out28(w28), .out29(w29), .out30(w30), .out31(w31), .sel(A3));  // open: en
  Register #(.width(32)) register_9 (.D(multiplexer_8_out), .Q(reg8), .clk(we_t), .clr(reset));  // open: en
  Multiplexer #(.width(32)) multiplexer_8 (.in0(reg8), .in1(WD), .out(multiplexer_8_out), .sel(w8));  // open: en
  Multiplexer #(.width(32)) multiplexer_9 (.in0(reg9), .in1(WD), .out(multiplexer_9_out), .sel(w9));  // open: en
  Register #(.width(32)) register_10 (.D(multiplexer_9_out), .Q(reg9), .clk(we_t), .clr(reset));  // open: en
  Register #(.width(32)) register_11 (.D(multiplexer_10_out), .Q(reg10), .clk(we_t), .clr(reset));  // open: en
  Multiplexer #(.width(32)) multiplexer_10 (.in0(reg10), .in1(WD), .out(multiplexer_10_out), .sel(w10));  // open: en
  Multiplexer #(.width(32)) multiplexer_11 (.in0(reg11), .in1(WD), .out(multiplexer_11_out), .sel(w11));  // open: en
  Register #(.width(32)) register_12 (.D(multiplexer_11_out), .Q(reg11), .clk(we_t), .clr(reset));  // open: en
  Register #(.width(32)) register_13 (.D(multiplexer_12_out), .Q(reg12), .clk(we_t), .clr(reset));  // open: en
  Multiplexer #(.width(32)) multiplexer_12 (.in0(reg12), .in1(WD), .out(multiplexer_12_out), .sel(w12));  // open: en
  Register #(.width(32)) register_14 (.D(multiplexer_13_out), .Q(reg13), .clk(we_t), .clr(reset));  // open: en
  Multiplexer #(.width(32)) multiplexer_13 (.in0(reg13), .in1(WD), .out(multiplexer_13_out), .sel(w13));  // open: en
  Multiplexer #(.width(32)) multiplexer_14 (.in0(reg14), .in1(WD), .out(multiplexer_14_out), .sel(w14));  // open: en
  Register #(.width(32)) register_15 (.D(multiplexer_14_out), .Q(reg14), .clk(we_t), .clr(reset));  // open: en
  Multiplexer #(.width(32)) multiplexer_15 (.in0(reg15), .in1(WD), .out(multiplexer_15_out), .sel(w15));  // open: en
  Register #(.width(32)) register_16 (.D(multiplexer_15_out), .Q(reg15), .clk(we_t), .clr(reset));  // open: en
  Multiplexer #(.width(32)) multiplexer_16 (.in0(reg16), .in1(WD), .out(multiplexer_16_out), .sel(w16));  // open: en
  Multiplexer #(.width(32)) multiplexer_17 (.in0(reg17), .in1(WD), .out(multiplexer_17_out), .sel(w17));  // open: en
  Multiplexer #(.width(32)) multiplexer_18 (.in0(reg18), .in1(WD), .out(multiplexer_18_out), .sel(w18));  // open: en
  Multiplexer #(.width(32)) multiplexer_19 (.in0(reg19), .in1(WD), .out(multiplexer_19_out), .sel(w19));  // open: en
  Multiplexer #(.width(32)) multiplexer_20 (.in0(reg20), .in1(WD), .out(multiplexer_20_out), .sel(w20));  // open: en
  Multiplexer #(.width(32)) multiplexer_21 (.in0(reg21), .in1(WD), .out(multiplexer_21_out), .sel(w21));  // open: en
  Multiplexer #(.width(32)) multiplexer_22 (.in0(reg22), .in1(WD), .out(multiplexer_22_out), .sel(w22));  // open: en
  Multiplexer #(.width(32)) multiplexer_23 (.in0(reg23), .in1(WD), .out(multiplexer_23_out), .sel(w23));  // open: en
  Multiplexer #(.select(5), .width(32)) multiplexer_24 (
    .in0(reg0), .in1(reg1), .in2(reg2), .in3(reg3), .in4(reg4), .in5(reg5), .in6(reg6), .in7(reg7),
    .in8(reg8), .in9(reg9), .in10(reg10), .in11(reg11), .in12(reg12), .in13(reg13), .in14(reg14),
    .in15(reg15), .in16(reg16), .in17(reg17), .in18(reg18), .in19(reg19), .in20(reg20), .in21(reg21),
    .in22(reg22), .in23(reg23), .in24(reg24), .in25(reg25), .in26(reg26), .in27(reg27), .in28(reg28),
    .in29(reg29), .in30(reg30), .in31(reg31), .out(RD1), .sel(A1));  // open: en
  Register #(.width(32)) register_17 (.D(multiplexer_16_out), .Q(reg16), .clk(we_t), .clr(reset));  // open: en
  Register #(.width(32)) register_18 (.D(multiplexer_17_out), .Q(reg17), .clk(we_t), .clr(reset));  // open: en
  Register #(.width(32)) register_19 (.D(multiplexer_18_out), .Q(reg18), .clk(we_t), .clr(reset));  // open: en
  Register #(.width(32)) register_20 (.D(multiplexer_19_out), .Q(reg19), .clk(we_t), .clr(reset));  // open: en
  Register #(.width(32)) register_21 (.D(multiplexer_20_out), .Q(reg20), .clk(we_t), .clr(reset));  // open: en
  Register #(.width(32)) register_22 (.D(multiplexer_21_out), .Q(reg21), .clk(we_t), .clr(reset));  // open: en
  Register #(.width(32)) register_23 (.D(multiplexer_22_out), .Q(reg22), .clk(we_t), .clr(reset));  // open: en
  Register #(.width(32)) register_24 (.D(multiplexer_23_out), .Q(reg23), .clk(we_t), .clr(reset));  // open: en
  Multiplexer #(.width(32)) multiplexer_25 (.in0(reg24), .in1(WD), .out(multiplexer_25_out), .sel(w24));  // open: en
  Multiplexer #(.width(32)) multiplexer_26 (.in0(reg25), .in1(WD), .out(multiplexer_26_out), .sel(w25));  // open: en
  Multiplexer #(.width(32)) multiplexer_27 (.in0(reg26), .in1(WD), .out(multiplexer_27_out), .sel(w26));  // open: en
  Multiplexer #(.width(32)) multiplexer_28 (.in0(reg27), .in1(WD), .out(multiplexer_28_out), .sel(w27));  // open: en
  Multiplexer #(.width(32)) multiplexer_29 (.in0(reg28), .in1(WD), .out(multiplexer_29_out), .sel(w28));  // open: en
  Multiplexer #(.width(32)) multiplexer_30 (.in0(reg29), .in1(WD), .out(multiplexer_30_out), .sel(w29));  // open: en
  Multiplexer #(.width(32)) multiplexer_31 (.in0(reg30), .in1(WD), .out(multiplexer_31_out), .sel(w30));  // open: en
  Multiplexer #(.width(32)) multiplexer_32 (.in0(reg31), .in1(WD), .out(multiplexer_32_out), .sel(w31));  // open: en
  Multiplexer #(.select(5), .width(32)) multiplexer_33 (
    .in0(reg0), .in1(reg1), .in2(reg2), .in3(reg3), .in4(reg4), .in5(reg5), .in6(reg6), .in7(reg7),
    .in8(reg8), .in9(reg9), .in10(reg10), .in11(reg11), .in12(reg12), .in13(reg13), .in14(reg14),
    .in15(reg15), .in16(reg16), .in17(reg17), .in18(reg18), .in19(reg19), .in20(reg20), .in21(reg21),
    .in22(reg22), .in23(reg23), .in24(reg24), .in25(reg25), .in26(reg26), .in27(reg27), .in28(reg28),
    .in29(reg29), .in30(reg30), .in31(reg31), .out(RD2), .sel(A2));  // open: en
  Register #(.width(32)) register_25 (.D(multiplexer_25_out), .Q(reg24), .clk(we_t), .clr(reset));  // open: en
  Register #(.width(32)) register_26 (.D(multiplexer_26_out), .Q(reg25), .clk(we_t), .clr(reset));  // open: en
  Register #(.width(32)) register_27 (.D(multiplexer_27_out), .Q(reg26), .clk(we_t), .clr(reset));  // open: en
  Register #(.width(32)) register_28 (.D(multiplexer_28_out), .Q(reg27), .clk(we_t), .clr(reset));  // open: en
  Register #(.width(32)) register_29 (.D(multiplexer_29_out), .Q(reg28), .clk(we_t), .clr(reset));  // open: en
  Register #(.width(32)) register_30 (.D(multiplexer_30_out), .Q(reg29), .clk(we_t), .clr(reset));  // open: en
  Register #(.width(32)) register_31 (.D(multiplexer_31_out), .Q(reg30), .clk(we_t), .clr(reset));  // open: en
  Register #(.width(32)) register_32 (.D(multiplexer_32_out), .Q(reg31), .clk(we_t), .clr(reset));  // open: en
endmodule
