// Logisim project P0_L1_ftoi.circ as structural Verilog: 1 circuit, main circuit ftoi
module ftoi (
  input  [15:0] float,
  output [31:0] \int 
);

  wire comparator_1_eq, comparator_3_eq, Den, Inf, NaN, Nor, not_1_out, right_shift, Zero;
  wire [4:0] shift;
  wire [31:0] abs, bit_extender_1_out, shifter_1_out, subtractor_2_out, val;

  Comparator #(.width(5), .mode("unsigned")) comparator_1 (
    .a({5{1'b1}}), .b(float[14:10]), .eq(comparator_1_eq));  // open: gt, lt
  Comparator #(.width(5), .mode("unsigned")) comparator_2 (.a(float[14:10]), .b({5{1'b0}}), .eq(Den));  // open: gt, lt
  Comparator #(.width(10), .mode("unsigned")) comparator_3 (
    .a(float[9:0]), .b({10{1'b0}}), .eq(comparator_3_eq));  // open: gt, lt
  not not_1 (not_1_out, comparator_3_eq);
  or or_1 (Zero, Inf, NaN, Den, right_shift);
  and and_1 (Inf, comparator_1_eq, comparator_3_eq);
  and and_2 (NaN, comparator_1_eq, not_1_out);
  not not_2 (Nor, Zero);
  Subtractor #(.width(5)) subtractor_1 (.a(float[14:10]), .b(5'b01111), .out(shift), .bout(right_shift));  // open: bin
  assign bit_extender_1_out = {{21{1'b0}}, {1'b1, float[9:0]}};  // Bit_Extender bit_extender_1
  Subtractor #(.width(32)) subtractor_2 (.a({32{1'b0}}), .b(abs), .out(subtractor_2_out));  // open: bin, bout
  Multiplexer #(.width(32)) multiplexer_1 (.in0(val), .in1({32{1'b0}}), .out(\int ), .sel(Zero));  // open: en
  Shifter #(.width(32)) shifter_1 (.in(bit_extender_1_out), .\dist (shift), .out(shifter_1_out));
  Multiplexer #(.width(32)) multiplexer_2 (.in0(abs), .in1(subtractor_2_out), .out(val), .sel(float[15]));  // open: en
  Shifter #(.width(32), .shift("lr")) shifter_2 (.in(shifter_1_out), .\dist (5'b01010), .out(abs));

  // Other names for the same wires on the sheet: base[9:0] = float[9:0]; f[9:0] = float[9:0]; input[15:0] = float;
  //   e[4:0] = float[14:10]; s = float[15]; output[31:0] = \int 
endmodule
