// Logisim project P0_L1_navigation_2020.circ as structural Verilog: 6 circuits, main circuit navigation
module navigation (
  input  clk,
  input  [1:0] dir,
  input  reset,
  output arrive,
  output hit
);

  wire status_storage_1_hit_2, status_trans_1_if_hit;
  wire [2:0] status_storage_1_status, status_trans_1_next_status;

  // Probe on status_storage_1_status
  status_trans status_trans_1 (
    .status(status_storage_1_status), .direction(dir), .hit_status(status_storage_1_hit_2),
    .next_status(status_trans_1_next_status), .if_hit(status_trans_1_if_hit));
  // Probe on status_trans_1_next_status
  status_storage status_storage_1 (
    .clk(clk), .next_status(status_trans_1_next_status), .hit(status_trans_1_if_hit), .reset(reset),
    .status(status_storage_1_status), .hit_2(status_storage_1_hit_2));
  \output  output_1 (.status(status_storage_1_status), .hit(status_storage_1_hit_2), .arrive(arrive), .hit_2(hit));
endmodule

module status_trans (
  input  [2:0] status,
  input  [1:0] direction,
  input  hit_status,
  output [2:0] next_status,
  output if_hit
);

  wire _0, _1, _2, _3, _4, and_1_out, and_2_out, and_3_out, and_4_out, and_7_out, and_8_out, e, n, s, to0,
       to1, to2, to3, to4, w;
  wire [2:0] next_spot;

  and and_1 (and_1_out, _1, s);
  and and_2 (and_2_out, _0, n);
  and and_3 (and_3_out, _2, w);
  and and_4 (and_4_out, _3, s);
  or or_1 (to0, and_1_out, _4);
  or or_2 (to1, and_2_out, and_3_out, and_4_out);
  and and_5 (to2, _1, e);
  and and_6 (to3, _1, n);
  and and_7 (and_7_out, _2, n);
  and and_8 (and_8_out, _3, e);
  Comparator #(.width(2), .mode("unsigned")) comparator_1 (.a(direction), .b(2'b00), .eq(n));  // open: gt, lt
  Comparator #(.width(2), .mode("unsigned")) comparator_2 (.a(direction), .b(2'b01), .eq(e));  // open: gt, lt
  Comparator #(.width(2), .mode("unsigned")) comparator_3 (.a(direction), .b(2'b10), .eq(s));  // open: gt, lt
  Comparator #(.width(2), .mode("unsigned")) comparator_4 (.a(direction), .b(2'b11), .eq(w));  // open: gt, lt
  or or_3 (to4, and_7_out, and_8_out);
  Decoder #(.select(3)) decoder_1 (
    .out0(_0), .out1(_1), .out2(_2), .out3(_3), .out4(_4), .sel(status));  // open: out5, out6, out7, en
  nor nor_1 (if_hit, to0, to1, to2, to3, to4);
  // Probe on next_spot
  BitFinder bitfinder_1 (.in({3'b111, to4, to3, to2, to1, to0}), .index(next_spot));  // open: found
  Multiplexer #(.select(3), .width(3)) multiplexer_1 (
    .in0(3'b000), .in1(3'b001), .in2(3'b010), .in3(3'b011), .in4(3'b100), .in5(status), .in6(status),
    .in7(status), .out(next_status), .sel(next_spot));  // open: en

  // Other names for the same wires on the sheet: dir[1:0] = direction

  // Notes on the sheet:
  //   to location 0
  //   to location 1
  //   to location 2
  //   to location 3
  //   to location 4
  //   output if_hit
  //   map:
  //   3     4
  //   1     2
  //   0
endmodule

module status_storage (
  input  clk,
  input  [2:0] next_status,
  input  hit,
  input  reset,
  output [2:0] status,
  output hit_2
);

  Register #(.width(3)) u_status (.D(next_status), .Q(status), .clk(clk), .clr(reset));  // open: en
  Register #(.width(1)) if_hit (.D(hit), .Q(hit_2), .clk(clk), .clr(reset));  // open: en
endmodule

module test (
  input  [2:0] in_1,
  input  in_2,
  input  in_3
);

  wire clock_1_out, status_storage_1_hit_2;
  wire [2:0] status_storage_1_status;

  Clock clock_1 (.out(clock_1_out));
  status_storage status_storage_1 (
    .clk(clock_1_out), .next_status(in_1), .hit(in_2), .reset(in_3), .status(status_storage_1_status),
    .hit_2(status_storage_1_hit_2));
  // Probe on status_storage_1_status
  // Probe on status_storage_1_hit_2
endmodule

module \output  (
  input  [2:0] status,
  input  hit,
  output arrive,
  output hit_2
);

  Comparator #(.width(3), .mode("unsigned")) comparator_1 (.a(3'b100), .b(status), .eq(arrive));  // open: gt, lt

  assign hit_2 = hit;

  // Other names for the same wires on the sheet: reach_B = arrive
endmodule

module bak_trans (
  input  [2:0] status,
  input  [1:0] direction,
  input  hit_status,
  output [2:0] next_status,
  output if_hit
);

  wire _0, _1, _2, _3, _4, and_2_out, and_3_out, and_4_out, and_5_out, and_6_out, and_7_out, and_8_out,
       and_9_out, and_10_out, e, n, s, to0, to1, to2, to3, to4, w;
  wire [2:0] next_spot;

  and and_1 (to0, _1, s);
  and and_2 (and_2_out, _0, n);
  and and_3 (and_3_out, _2, w);
  and and_4 (and_4_out, _3, s);
  or or_1 (to1, and_2_out, and_3_out, and_4_out);
  and and_5 (and_5_out, _1, e);
  and and_6 (and_6_out, _4, s);
  and and_7 (and_7_out, _1, n);
  and and_8 (and_8_out, _4, w);
  Comparator #(.width(2), .mode("unsigned")) comparator_1 (.a(direction), .b(2'b00), .eq(n));  // open: gt, lt
  Comparator #(.width(2), .mode("unsigned")) comparator_2 (.a(direction), .b(2'b01), .eq(e));  // open: gt, lt
  Comparator #(.width(2), .mode("unsigned")) comparator_3 (.a(direction), .b(2'b10), .eq(s));  // open: gt, lt
  Comparator #(.width(2), .mode("unsigned")) comparator_4 (.a(direction), .b(2'b11), .eq(w));  // open: gt, lt
  or or_2 (to2, and_5_out, and_6_out);
  or or_3 (to3, and_7_out, and_8_out);
  Decoder #(.select(3)) decoder_1 (
    .out0(_0), .out1(_1), .out2(_2), .out3(_3), .out4(_4), .sel(status));  // open: out5, out6, out7, en
  and and_9 (and_9_out, _2, n);
  or or_4 (to4, and_9_out, and_10_out);
  and and_10 (and_10_out, _3, e);
  nor nor_1 (if_hit, to0, to1, to2, to3, to4);
  // Probe on next_spot
  BitFinder bitfinder_1 (.in({3'b111, to4, to3, to2, to1, to0}), .index(next_spot));  // open: found
  Multiplexer #(.select(3), .width(3)) multiplexer_1 (
    .in0(3'b000), .in1(3'b001), .in2(3'b010), .in3(3'b011), .in4(3'b100), .in5(status), .in6(status),
    .in7(status), .out(next_status), .sel(next_spot));  // open: en

  // Other names for the same wires on the sheet: dir[1:0] = direction

  // Notes on the sheet:
  //   to location 0
  //   to location 1
  //   to location 2
  //   to location 3
  //   to location 4
  //   output if_hit
  //   map:
  //   3     4
  //   1     2
  //   0
endmodule
