// Logisim project P0_L2_nonexist_2023.circ as structural Verilog: 2 circuits, main circuit main
module main (
  input  [7:0] _1,
  input  [7:0] _2,
  input  [7:0] _3,
  input  [7:0] _4,
  input  [7:0] _5,
  output [7:0] out_6
);

  wire is1, is2, is3, is4, is5, is6;
  wire [7:0] multiplexer_1_out, multiplexer_2_out, multiplexer_3_out, multiplexer_4_out, multiplexer_5_out;

  judge judge_1 (.\input (8'h1), ._1(_1), ._2(_2), ._3(_3), ._4(_4), ._5(_5), .judge(is1));
  judge judge_2 (.\input (8'h4), ._1(_1), ._2(_2), ._3(_3), ._4(_4), ._5(_5), .judge(is4));
  Multiplexer #(.width(8)) multiplexer_1 (.in1(8'h6), .out(multiplexer_1_out), .sel(is6));  // open: in0, en
  Multiplexer #(.width(8)) multiplexer_2 (
    .in0(multiplexer_1_out), .in1(8'h5), .out(multiplexer_2_out), .sel(is5));  // open: en
  Multiplexer #(.width(8)) multiplexer_3 (
    .in0(multiplexer_2_out), .in1(8'h4), .out(multiplexer_3_out), .sel(is4));  // open: en
  judge judge_3 (.\input (8'h2), ._1(_1), ._2(_2), ._3(_3), ._4(_4), ._5(_5), .judge(is2));
  judge judge_4 (.\input (8'h5), ._1(_1), ._2(_2), ._3(_3), ._4(_4), ._5(_5), .judge(is5));
  Multiplexer #(.width(8)) multiplexer_4 (
    .in0(multiplexer_3_out), .in1(8'h3), .out(multiplexer_4_out), .sel(is3));  // open: en
  Multiplexer #(.width(8)) multiplexer_5 (
    .in0(multiplexer_4_out), .in1(8'h2), .out(multiplexer_5_out), .sel(is2));  // open: en
  judge judge_5 (.\input (8'h3), ._1(_1), ._2(_2), ._3(_3), ._4(_4), ._5(_5), .judge(is3));
  judge judge_6 (.\input (8'h6), ._1(_1), ._2(_2), ._3(_3), ._4(_4), ._5(_5), .judge(is6));
  Multiplexer #(.width(8)) multiplexer_6 (.in0(multiplexer_5_out), .in1(8'h1), .out(out_6), .sel(is1));  // open: en

  // Other names for the same wires on the sheet: out[7:0] = out_6
endmodule

module judge (
  input  [7:0] \input ,
  input  [7:0] _1,
  input  [7:0] _2,
  input  [7:0] _3,
  input  [7:0] _4,
  input  [7:0] _5,
  output judge
);

  wire comparator_1_eq, comparator_2_eq, comparator_3_eq, comparator_4_eq, comparator_5_eq, or_1_out;

  Comparator #(.mode("unsigned")) comparator_1 (.a(_1), .b(\input ), .eq(comparator_1_eq));  // open: gt, lt
  Comparator #(.mode("unsigned")) comparator_2 (.a(_2), .b(\input ), .eq(comparator_2_eq));  // open: gt, lt
  Comparator #(.mode("unsigned")) comparator_3 (.a(_3), .b(\input ), .eq(comparator_3_eq));  // open: gt, lt
  Comparator #(.mode("unsigned")) comparator_4 (.a(_4), .b(\input ), .eq(comparator_4_eq));  // open: gt, lt
  Comparator #(.mode("unsigned")) comparator_5 (.a(_5), .b(\input ), .eq(comparator_5_eq));  // open: gt, lt
  or or_1 (or_1_out, comparator_1_eq, comparator_2_eq, comparator_3_eq, comparator_4_eq, comparator_5_eq);
  not not_1 (judge, or_1_out);
endmodule
