// Logisim project P0_L3_walker_2023.circ as structural Verilog: 4 circuits, main circuit main
module main (
  input  [1:0] \input ,
  input  reset,
  input  clk,
  output [3:0] out_4
);

  wire [2:0] store_1_out_4, trans_1_next_state;

  trans trans_1 (.state(store_1_out_4), .\input (\input ), .next_state(trans_1_next_state));
  store store_1 (.in_1(trans_1_next_state), .clk(clk), .reset(reset), .out_4(store_1_out_4));
  \output  output_1 (.\input (\input ), .state(store_1_out_4), .\output (out_4));
endmodule

module \output  (
  input  [1:0] \input ,
  input  [2:0] state,
  output [3:0] \output 
);

  wire [2:0] trans_1_next_state;
  wire [3:0] bit_extender_1_out;

  trans trans_1 (.state(state), .\input (\input ), .next_state(trans_1_next_state));
  assign bit_extender_1_out = {{1{1'b0}}, trans_1_next_state};  // Bit_Extender bit_extender_1
  Adder #(.width(4)) adder_1 (.a(bit_extender_1_out), .b(4'b0001), .out(\output ));  // open: cin, cout
endmodule

module store (
  input  [2:0] in_1,
  input  clk,
  input  reset,
  output [2:0] out_4
);

  Register #(.width(3)) register_1 (.D(in_1), .Q(out_4), .clk(clk), .clr(reset));  // open: en
endmodule

module trans (
  input  [2:0] state,
  input  [1:0] \input ,
  output [2:0] next_state
);

  wire and_1_out, and_2_out, and_3_out, and_4_out, and_5_out, and_6_out, and_7_out, and_8_out, and_9_out,
       and_10_out, and_11_out, and_12_out, and_13_out, and_14_out, and_15_out, and_16_out, and_17_out,
       and_18_out, and_19_out, and_20_out, not_1_out, not_2_out, not_3_out, not_4_out, not_5_out, not_6_out,
       not_7_out, not_8_out, not_9_out, not_10_out, not_11_out, not_12_out, not_13_out, not_14_out,
       not_15_out, not_16_out, not_17_out, not_18_out, not_19_out, not_20_out, not_21_out, not_22_out,
       not_23_out, not_24_out, not_25_out, not_26_out, not_27_out, not_28_out, not_29_out, not_30_out,
       not_31_out, not_32_out, not_33_out, not_34_out, not_35_out, not_36_out;

  not not_1 (not_1_out, state[1]);
  not not_2 (not_2_out, state[0]);
  not not_3 (not_3_out, \input [0]);
  not not_4 (not_4_out, \input [0]);
  not not_5 (not_5_out, state[2]);
  not not_6 (not_6_out, state[0]);
  not not_7 (not_7_out, \input [0]);
  not not_8 (not_8_out, state[2]);
  not not_9 (not_9_out, \input [1]);
  not not_10 (not_10_out, state[0]);
  not not_11 (not_11_out, \input [1]);
  not not_12 (not_12_out, \input [0]);
  not not_13 (not_13_out, state[2]);
  not not_14 (not_14_out, state[1]);
  not not_15 (not_15_out, state[0]);
  not not_16 (not_16_out, \input [1]);
  not not_17 (not_17_out, state[2]);
  not not_18 (not_18_out, state[1]);
  not not_19 (not_19_out, \input [0]);
  not not_20 (not_20_out, state[2]);
  not not_21 (not_21_out, state[0]);
  not not_22 (not_22_out, \input [0]);
  not not_23 (not_23_out, state[1]);
  not not_24 (not_24_out, state[0]);
  not not_25 (not_25_out, \input [1]);
  not not_26 (not_26_out, \input [0]);
  not not_27 (not_27_out, state[1]);
  not not_28 (not_28_out, state[0]);
  and and_1 (and_1_out, not_1_out, not_2_out, \input [1], not_3_out);
  and and_2 (and_2_out, state[1], state[0], \input [1], not_4_out);
  and and_3 (and_3_out, state[2], not_29_out);
  not not_29 (not_29_out, \input [1]);
  and and_4 (and_4_out, state[2], not_30_out, state[0]);
  not not_30 (not_30_out, state[1]);
  and and_5 (and_5_out, state[2], state[1], not_31_out);
  not not_31 (not_31_out, state[0]);
  and and_6 (and_6_out, not_5_out, not_6_out, \input [1], not_7_out);
  and and_7 (and_7_out, not_8_out, state[0], not_9_out, \input [0]);
  not not_32 (not_32_out, state[2]);
  and and_8 (and_8_out, not_32_out, state[1], \input [0]);
  and and_9 (and_9_out, state[1], state[0], not_33_out);
  not not_33 (not_33_out, \input [1]);
  and and_10 (and_10_out, state[2], not_10_out, \input [1], \input [0]);
  and and_11 (and_11_out, state[2], state[0], not_11_out, not_12_out);
  and and_12 (and_12_out, state[2], state[1], not_34_out);
  not not_34 (not_34_out, \input [0]);
  and and_13 (and_13_out, not_13_out, not_14_out, not_15_out, not_16_out, \input [0]);
  and and_14 (and_14_out, not_17_out, not_18_out, \input [1], not_19_out);
  not not_35 (not_35_out, state[1]);
  and and_15 (and_15_out, not_35_out, state[0], \input [1]);
  and and_16 (and_16_out, not_20_out, state[1], not_21_out, not_22_out);
  and and_17 (and_17_out, state[1], state[0], not_36_out);
  not not_36 (not_36_out, \input [1]);
  and and_18 (and_18_out, state[2], not_23_out, not_24_out, not_25_out, not_26_out);
  and and_19 (and_19_out, state[2], not_27_out, \input [1], \input [0]);
  and and_20 (and_20_out, state[2], state[1], not_28_out, \input [0]);
  or or_1 (next_state[2], and_1_out, and_2_out, and_3_out, and_4_out, and_5_out);
  or or_2 (next_state[1], and_6_out, and_7_out, and_8_out, and_9_out, and_10_out, and_11_out, and_12_out);
  or or_3 (next_state[0], and_13_out, and_14_out, and_15_out, and_16_out, and_17_out, and_18_out, and_19_out, and_20_out);

  // Other names for the same wires on the sheet: n0 = next_state[0]; n1 = next_state[1]; n2 = next_state[2]
endmodule
