// Logisim project P3.circ as structural Verilog
module main (
  input  rst,
  output [31:0] out_2,
  output [31:0] out_3,
  output out_4,
  output [4:0] out_5,
  output [31:0] out_6,
  output out_7,
  output [31:0] out_8,
  output [31:0] out_9
);

  wire ALU_zf, clk, control_unit_1_alusrc, control_unit_1_branch, control_unit_1_extop,
       control_unit_1_memread, control_unit_1_memtoreg, control_unit_1_regdst, IfBranch, IfJump;
  wire [3:0] control_unit_1_aluop;
  wire [4:0] splitter_1_rd, splitter_1_rs, splitter_1_rt;
  wire [5:0] Funct, Opcode;
  wire [15:0] splitter_1_imm;
  wire [25:0] Offset26;
  wire [31:0] dm_32bit_1_out, ext_1_out, GRF_rd1, multiplexer_2_out;

  Clock clock_1 (.out(clk));
  IFU ifu_1 (
    .ifBranch(IfBranch), .Offset16(splitter_1_imm), .clk(clk), .Rst(rst), .InsOut(out_2), .PC(out_3),
    .ifJump(IfJump), .Offset26(Offset26));  // open: ra, ifJr
  Splitter splitter_1 (
    .Ins(out_2), .Opcode(Opcode), .rs(splitter_1_rs), .rt(splitter_1_rt), .rd(splitter_1_rd),
    .Imm(splitter_1_imm), .InsAddr(Offset26), .Func(Funct));  // open: s
  Multiplexer #(.width(5)) multiplexer_1 (
    .in0(splitter_1_rt), .in1(splitter_1_rd), .out(out_5), .sel(control_unit_1_regdst));  // open: en
  Control_Unit control_unit_1 (
    .Op(Opcode), .ALUSrc(control_unit_1_alusrc), .MemtoReg(control_unit_1_memtoreg), .RegWrite(out_4),
    .MemRead(control_unit_1_memread), .MemWrite(out_7), .Branch(control_unit_1_branch),
    .RegDst(control_unit_1_regdst), .ALUOp(control_unit_1_aluop), .Func(Funct), .ExtOp(control_unit_1_extop),
    .Jump(IfJump));
  GRF GRF (
    .clk(clk), .reset(rst), .WE(out_4), .A1(splitter_1_rs), .A2(splitter_1_rt), .A3(out_5), .WD(out_6),
    .RD1(GRF_rd1), .RD2(out_9));
  Ext ext_1 (.In(splitter_1_imm), .Out(ext_1_out), .ExtOp(control_unit_1_extop));
  Multiplexer #(.width(32)) multiplexer_2 (
    .in0(out_9), .in1(ext_1_out), .out(multiplexer_2_out), .sel(control_unit_1_alusrc));  // open: en
  // Probe on multiplexer_2_out
  // Probe on GRF_rd1
  ALU ALU (.A(GRF_rd1), .B(multiplexer_2_out), .ZF(ALU_zf), .Result(out_8), .ALUOp(control_unit_1_aluop));
  and and_1 (IfBranch, control_unit_1_branch, ALU_zf);
  DM_32bit dm_32bit_1 (
    .clk(clk), .RE(control_unit_1_memread), .WE(out_7), .DataAddr(out_8), .WriteData(out_9),
    .Out(dm_32bit_1_out), .rst(rst));
  Multiplexer #(.width(32)) multiplexer_3 (
    .in0(out_8), .in1(dm_32bit_1_out), .out(out_6), .sel(control_unit_1_memtoreg));  // open: en

  // Other names for the same wires on the sheet: Instr[31:0] = out_2; MemAddr[31:0] = out_8; MemData[31:0] = out_9;
  //   MemWrite = out_7; PC[31:0] = out_3; RegAddr[4:0] = out_5; RegData[31:0] = out_6; RegWrite = out_4
endmodule

module IFU (
  input  ifBranch,
  input  [15:0] Offset16,
  input  clk,
  input  Rst,
  input  ifJump,
  input  ifJr,
  input  [25:0] Offset26,
  input  [31:0] ra,
  output [31:0] PC,
  output [31:0] InsOut
);

  wire [11:0] bitselector_1_out;
  wire [27:0] bit_extender_2_out, Offset26_t, shifter_4_out;
  wire [31:0] adder_2_out, adder_3_out, adder_4_out, bit_extender_1_out, multiplexer_1_out, nextPC,
       Offset16_t, register_1_q, shifter_3_out, subtractor_1_out;
  wire [31:28] shifter_4_out_2;

  assign bit_extender_1_out = {{16{Offset16[15]}}, Offset16};  // Bit_Extender bit_extender_1
  assign bit_extender_2_out = {{2{Offset26[25]}}, Offset26};  // Bit_Extender bit_extender_2
  Subtractor #(.width(32)) subtractor_1 (.a(nextPC), .b(32'h3000), .out(subtractor_1_out));  // open: bin, bout
  Shifter #(.width(32)) shifter_1 (.in(bit_extender_1_out), .\dist (5'b00010), .out(Offset16_t));
  Shifter #(.width(28)) shifter_2 (.in(bit_extender_2_out), .\dist (5'b00010), .out(Offset26_t));
  Shifter #(.width(32), .shift("lr")) shifter_3 (.in(subtractor_1_out), .\dist (5'b00010), .out(shifter_3_out));
  // Probe on shifter_3_out
  Register #(.width(32)) register_1 (.D(shifter_3_out), .Q(register_1_q), .clk(clk), .clr(Rst));  // open: en
  Shifter #(.width(32)) shifter_4 (.in(register_1_q), .\dist (5'b00010), .out({shifter_4_out_2, shifter_4_out}));
  BitSelector #(.width(32), .group(12)) bitselector_1 (.in(register_1_q), .out(bitselector_1_out), .sel(2'b00));
  Adder #(.width(32)) adder_1 (.a({shifter_4_out_2, shifter_4_out}), .b(32'h3000), .out(PC));  // open: cin, cout
  Adder #(.width(32)) adder_2 (.a({shifter_4_out_2, shifter_4_out}), .b(32'h4), .out(adder_2_out));  // open: cin, cout
  ROM #(.addrWidth(12), .dataWidth(32)) rom_1 (.addr(bitselector_1_out), .data(InsOut), .sel(1'b1));
  Multiplexer #(.width(32)) multiplexer_1 (
    .in0(adder_2_out), .in1(adder_3_out), .out(multiplexer_1_out), .sel(ifBranch));  // open: en
  Adder #(.width(32)) adder_3 (.a(adder_2_out), .b(Offset16_t), .out(adder_3_out));  // open: cin, cout
  Adder #(.width(32)) adder_4 (.a(multiplexer_1_out), .b(32'h3000), .out(adder_4_out));  // open: cin, cout
  Multiplexer #(.width(32)) multiplexer_2 (
    .in0(adder_4_out), .in1({shifter_4_out_2, Offset26_t}), .out(nextPC), .sel(ifJump));  // open: en
  Pull_Resistor pull_resistor_1 (.node(ifJump));

  // Notes on the sheet:
  //   contents of rom_1 (hex, n*v repeats v):
  //   3404007b 348501c8 3c06007b 3c07ffff 34e7ffff 868020 878820 e79020 34080004 ad04fffc ad040000
  //   ad050004 ad060008 ad07000c ad100010 ad110014 ad120018 8d040000 8d05000c ad04001c ad050020 34040001
  //   34050002 34060001 10850001 10860001 ad040024 ad050028
endmodule

module GRF (
  input  clk,
  input  reset,
  input  WE,
  input  [4:0] A1,
  input  [4:0] A2,
  input  [4:0] A3,
  input  [31:0] WD,
  output [31:0] RD1,
  output [31:0] RD2
);

  wire w0, w1, w2, w3, w4, w5, w6, w7, w8, w9, w10, w11, w12, w13, w14, w15, w16, w17, w18, w19, w20, w21,
       w22, w23, w24, w25, w26, w27, w28, w29, w30, w31;
  wire [31:0] multiplexer_1_out, multiplexer_2_out, multiplexer_3_out, multiplexer_4_out, multiplexer_5_out,
       multiplexer_6_out, multiplexer_7_out, multiplexer_8_out, multiplexer_9_out, multiplexer_10_out,
       multiplexer_11_out, multiplexer_12_out, multiplexer_13_out, multiplexer_14_out, multiplexer_15_out,
       multiplexer_16_out, multiplexer_17_out, multiplexer_18_out, multiplexer_19_out, multiplexer_20_out,
       multiplexer_21_out, multiplexer_22_out, multiplexer_23_out, multiplexer_25_out, multiplexer_26_out,
       multiplexer_27_out, multiplexer_28_out, multiplexer_29_out, multiplexer_30_out, multiplexer_31_out,
       multiplexer_32_out, reg0, reg1, reg2, reg3, reg4, reg5, reg6, reg7, reg8, reg9, reg10, reg11, reg12,
       reg13, reg14, reg15, reg16, reg17, reg18, reg19, reg20, reg21, reg22, reg23, reg24, reg25, reg26,
       reg27, reg28, reg29, reg30, reg31;

  Register #(.width(32)) register_1 (.D({32{1'b0}}), .en(WE), .Q(reg0), .clk(clk), .clr(reset));
  Multiplexer #(.width(32)) multiplexer_1 (.in0(reg1), .in1(WD), .out(multiplexer_1_out), .sel(w1));  // open: en
  Register #(.width(32)) register_2 (.D(multiplexer_1_out), .en(WE), .Q(reg1), .clk(clk), .clr(reset));
  Register #(.width(32)) register_3 (.D(multiplexer_2_out), .en(WE), .Q(reg2), .clk(clk), .clr(reset));
  Multiplexer #(.width(32)) multiplexer_2 (.in0(reg2), .in1(WD), .out(multiplexer_2_out), .sel(w2));  // open: en
  Register #(.width(32)) register_4 (.D(multiplexer_3_out), .en(WE), .Q(reg3), .clk(clk), .clr(reset));
  Multiplexer #(.width(32)) multiplexer_3 (.in0(reg3), .in1(WD), .out(multiplexer_3_out), .sel(w3));  // open: en
  Register #(.width(32)) register_5 (.D(multiplexer_4_out), .en(WE), .Q(reg4), .clk(clk), .clr(reset));
  Multiplexer #(.width(32)) multiplexer_4 (.in0(reg4), .in1(WD), .out(multiplexer_4_out), .sel(w4));  // open: en
  Register #(.width(32)) register_6 (.D(multiplexer_5_out), .en(WE), .Q(reg5), .clk(clk), .clr(reset));
  Multiplexer #(.width(32)) multiplexer_5 (.in0(reg5), .in1(WD), .out(multiplexer_5_out), .sel(w5));  // open: en
  Register #(.width(32)) register_7 (.D(multiplexer_6_out), .en(WE), .Q(reg6), .clk(clk), .clr(reset));
  Multiplexer #(.width(32)) multiplexer_6 (.in0(reg6), .in1(WD), .out(multiplexer_6_out), .sel(w6));  // open: en
  Multiplexer #(.width(32)) multiplexer_7 (.in0(reg7), .in1(WD), .out(multiplexer_7_out), .sel(w7));  // open: en
  Register #(.width(32)) register_8 (.D(multiplexer_7_out), .en(WE), .Q(reg7), .clk(clk), .clr(reset));
  Decoder #(.select(5)) decoder_1 (
    .out0(w0), .out1(w1), .out2(w2), .out3(w3), .out4(w4), .out5(w5), .out6(w6), .out7(w7), .out8(w8),
    .out9(w9), .out10(w10), .out11(w11), .out12(w12), .out13(w13), .out14(w14), .out15(w15), .out16(w16),
    .out17(w17), .out18(w18), .out19(w19), .out20(w20), .out21(w21), .out22(w22), .out23(w23), .out24(w24),
    .out25(w25), .out26(w26), .out27(w27), .out28(w28), .out29(w29), .out30(w30), .out31(w31), .sel(A3));  // open: en
  Multiplexer #(.width(32)) multiplexer_8 (.in0(reg8), .in1(WD), .out(multiplexer_8_out), .sel(w8));  // open: en
  Register #(.width(32)) register_9 (.D(multiplexer_8_out), .en(WE), .Q(reg8), .clk(clk), .clr(reset));
  Multiplexer #(.width(32)) multiplexer_9 (.in0(reg9), .in1(WD), .out(multiplexer_9_out), .sel(w9));  // open: en
  Register #(.width(32)) register_10 (.D(multiplexer_9_out), .en(WE), .Q(reg9), .clk(clk), .clr(reset));
  Register #(.width(32)) register_11 (.D(multiplexer_10_out), .en(WE), .Q(reg10), .clk(clk), .clr(reset));
  Multiplexer #(.width(32)) multiplexer_10 (.in0(reg10), .in1(WD), .out(multiplexer_10_out), .sel(w10));  // open: en
  Register #(.width(32)) register_12 (.D(multiplexer_11_out), .en(WE), .Q(reg11), .clk(clk), .clr(reset));
  Multiplexer #(.width(32)) multiplexer_11 (.in0(reg11), .in1(WD), .out(multiplexer_11_out), .sel(w11));  // open: en
  Register #(.width(32)) register_13 (.D(multiplexer_12_out), .en(WE), .Q(reg12), .clk(clk), .clr(reset));
  Multiplexer #(.width(32)) multiplexer_12 (.in0(reg12), .in1(WD), .out(multiplexer_12_out), .sel(w12));  // open: en
  Multiplexer #(.width(32)) multiplexer_13 (.in0(reg13), .in1(WD), .out(multiplexer_13_out), .sel(w13));  // open: en
  Register #(.width(32)) register_14 (.D(multiplexer_13_out), .en(WE), .Q(reg13), .clk(clk), .clr(reset));
  Register #(.width(32)) register_15 (.D(multiplexer_14_out), .en(WE), .Q(reg14), .clk(clk), .clr(reset));
  Multiplexer #(.width(32)) multiplexer_14 (.in0(reg14), .in1(WD), .out(multiplexer_14_out), .sel(w14));  // open: en
  Multiplexer #(.width(32)) multiplexer_15 (.in0(reg15), .in1(WD), .out(multiplexer_15_out), .sel(w15));  // open: en
  Register #(.width(32)) register_16 (.D(multiplexer_15_out), .en(WE), .Q(reg15), .clk(clk), .clr(reset));
  Multiplexer #(.width(32)) multiplexer_16 (.in0(reg16), .in1(WD), .out(multiplexer_16_out), .sel(w16));  // open: en
  Multiplexer #(.width(32)) multiplexer_17 (.in0(reg17), .in1(WD), .out(multiplexer_17_out), .sel(w17));  // open: en
  Multiplexer #(.width(32)) multiplexer_18 (.in0(reg18), .in1(WD), .out(multiplexer_18_out), .sel(w18));  // open: en
  Multiplexer #(.width(32)) multiplexer_19 (.in0(reg19), .in1(WD), .out(multiplexer_19_out), .sel(w19));  // open: en
  Multiplexer #(.width(32)) multiplexer_20 (.in0(reg20), .in1(WD), .out(multiplexer_20_out), .sel(w20));  // open: en
  Multiplexer #(.width(32)) multiplexer_21 (.in0(reg21), .in1(WD), .out(multiplexer_21_out), .sel(w21));  // open: en
  Multiplexer #(.width(32)) multiplexer_22 (.in0(reg22), .in1(WD), .out(multiplexer_22_out), .sel(w22));  // open: en
  Multiplexer #(.width(32)) multiplexer_23 (.in0(reg23), .in1(WD), .out(multiplexer_23_out), .sel(w23));  // open: en
  Multiplexer #(.select(5), .width(32)) multiplexer_24 (
    .in0(reg0), .in1(reg1), .in2(reg2), .in3(reg3), .in4(reg4), .in5(reg5), .in6(reg6), .in7(reg7),
    .in8(reg8), .in9(reg9), .in10(reg10), .in11(reg11), .in12(reg12), .in13(reg13), .in14(reg14),
    .in15(reg15), .in16(reg16), .in17(reg17), .in18(reg18), .in19(reg19), .in20(reg20), .in21(reg21),
    .in22(reg22), .in23(reg23), .in24(reg24), .in25(reg25), .in26(reg26), .in27(reg27), .in28(reg28),
    .in29(reg29), .in30(reg30), .in31(reg31), .out(RD1), .sel(A1));  // open: en
  Register #(.width(32)) register_17 (.D(multiplexer_16_out), .en(WE), .Q(reg16), .clk(clk), .clr(reset));
  Register #(.width(32)) register_18 (.D(multiplexer_17_out), .en(WE), .Q(reg17), .clk(clk), .clr(reset));
  Register #(.width(32)) register_19 (.D(multiplexer_18_out), .en(WE), .Q(reg18), .clk(clk), .clr(reset));
  Register #(.width(32)) register_20 (.D(multiplexer_19_out), .en(WE), .Q(reg19), .clk(clk), .clr(reset));
  Register #(.width(32)) register_21 (.D(multiplexer_20_out), .en(WE), .Q(reg20), .clk(clk), .clr(reset));
  Register #(.width(32)) register_22 (.D(multiplexer_21_out), .en(WE), .Q(reg21), .clk(clk), .clr(reset));
  Register #(.width(32)) register_23 (.D(multiplexer_22_out), .en(WE), .Q(reg22), .clk(clk), .clr(reset));
  Register #(.width(32)) register_24 (.D(multiplexer_23_out), .en(WE), .Q(reg23), .clk(clk), .clr(reset));
  Multiplexer #(.width(32)) multiplexer_25 (.in0(reg24), .in1(WD), .out(multiplexer_25_out), .sel(w24));  // open: en
  Multiplexer #(.width(32)) multiplexer_26 (.in0(reg25), .in1(WD), .out(multiplexer_26_out), .sel(w25));  // open: en
  Multiplexer #(.width(32)) multiplexer_27 (.in0(reg26), .in1(WD), .out(multiplexer_27_out), .sel(w26));  // open: en
  Multiplexer #(.width(32)) multiplexer_28 (.in0(reg27), .in1(WD), .out(multiplexer_28_out), .sel(w27));  // open: en
  Multiplexer #(.width(32)) multiplexer_29 (.in0(reg28), .in1(WD), .out(multiplexer_29_out), .sel(w28));  // open: en
  Multiplexer #(.width(32)) multiplexer_30 (.in0(reg29), .in1(WD), .out(multiplexer_30_out), .sel(w29));  // open: en
  Multiplexer #(.width(32)) multiplexer_31 (.in0(reg30), .in1(WD), .out(multiplexer_31_out), .sel(w30));  // open: en
  Multiplexer #(.width(32)) multiplexer_32 (.in0(reg31), .in1(WD), .out(multiplexer_32_out), .sel(w31));  // open: en
  Multiplexer #(.select(5), .width(32)) multiplexer_33 (
    .in0(reg0), .in1(reg1), .in2(reg2), .in3(reg3), .in4(reg4), .in5(reg5), .in6(reg6), .in7(reg7),
    .in8(reg8), .in9(reg9), .in10(reg10), .in11(reg11), .in12(reg12), .in13(reg13), .in14(reg14),
    .in15(reg15), .in16(reg16), .in17(reg17), .in18(reg18), .in19(reg19), .in20(reg20), .in21(reg21),
    .in22(reg22), .in23(reg23), .in24(reg24), .in25(reg25), .in26(reg26), .in27(reg27), .in28(reg28),
    .in29(reg29), .in30(reg30), .in31(reg31), .out(RD2), .sel(A2));  // open: en
  Register #(.width(32)) register_25 (.D(multiplexer_25_out), .en(WE), .Q(reg24), .clk(clk), .clr(reset));
  Register #(.width(32)) register_26 (.D(multiplexer_26_out), .en(WE), .Q(reg25), .clk(clk), .clr(reset));
  Register #(.width(32)) register_27 (.D(multiplexer_27_out), .en(WE), .Q(reg26), .clk(clk), .clr(reset));
  Register #(.width(32)) register_28 (.D(multiplexer_28_out), .en(WE), .Q(reg27), .clk(clk), .clr(reset));
  Register #(.width(32)) register_29 (.D(multiplexer_29_out), .en(WE), .Q(reg28), .clk(clk), .clr(reset));
  Register #(.width(32)) register_30 (.D(multiplexer_30_out), .en(WE), .Q(reg29), .clk(clk), .clr(reset));
  Register #(.width(32)) register_31 (.D(multiplexer_31_out), .en(WE), .Q(reg30), .clk(clk), .clr(reset));
  Register #(.width(32)) register_32 (.D(multiplexer_32_out), .en(WE), .Q(reg31), .clk(clk), .clr(reset));
endmodule

module ALU (
  input  [31:0] A,
  input  [31:0] B,
  input  [3:0] ALUOp,
  output ZF,
  output [31:0] Result
);

  wire [4:0] bitselector_1_out;
  wire [31:0] adder_1_out, or_1_out, shifter_1_out, shifter_2_out, subtractor_1_out, xor_1_out;

  BitSelector #(.width(32), .group(5)) bitselector_1 (.in(B), .out(bitselector_1_out), .sel(3'b000));
  Adder #(.width(32)) adder_1 (.a(A), .b(B), .out(adder_1_out));  // open: cin, cout
  Subtractor #(.width(32)) subtractor_1 (.a(A), .b(B), .out(subtractor_1_out));  // open: bin, bout
  assign or_1_out = A | B;  // OR_Gate or_1, 32 bits wide
  Shifter #(.width(32)) shifter_1 (.in(A), .\dist (bitselector_1_out), .out(shifter_1_out));
  Shifter #(.width(32)) shifter_2 (.in(B), .\dist (5'b10000), .out(shifter_2_out));
  assign xor_1_out = A ^ B;  // XOR_Gate xor_1, 32 bits wide
  Multiplexer #(.select(4), .width(32)) multiplexer_1 (
    .in0(adder_1_out), .in1(subtractor_1_out), .in2(or_1_out), .in3(shifter_1_out), .in4(shifter_2_out),
    .in5(xor_1_out), .out(Result), .sel(ALUOp));  // open: in6, in7, in8, in9, in10, in11, in12, in13, in14, in15, en
  Comparator #(.width(32)) comparator_1 (.a({32{1'b0}}), .b(Result), .eq(ZF));  // open: gt, lt

  // Other names for the same wires on the sheet: Zero = ZF
endmodule

module Control_Unit (
  input  [5:0] Op,
  input  [5:0] Func,
  output ALUSrc,
  output MemtoReg,
  output RegWrite,
  output MemRead,
  output MemWrite,
  output Branch,
  output [3:0] ALUOp,
  output RegDst,
  output ExtOp,
  output Jump
);

  wire add, beq, bitfinder_1_found, lui, lw, not_1_out, not_2_out, not_3_out, not_4_out, not_5_out,
       not_6_out, not_7_out, not_8_out, not_9_out, not_10_out, not_11_out, not_12_out, ori, sll, special,
       sub, sw;
  wire [1:0] or_2_out;
  wire [3:0] bitfinder_1_index;

  not not_1 (not_1_out, Op[5]);
  not not_2 (not_2_out, Op[4]);
  not not_3 (not_3_out, Op[3]);
  not not_4 (not_4_out, Op[2]);
  not not_5 (not_5_out, Op[0]);
  not not_6 (not_6_out, Op[1]);
  and and_1 (special, not_1_out, not_2_out, not_3_out, not_4_out, not_6_out, not_5_out);
  and and_2 (ori, not_1_out, not_2_out, Op[3], Op[2], not_6_out, Op[0]);
  and and_3 (lw, Op[5], not_2_out, not_3_out, not_4_out, Op[1], Op[0]);
  and and_4 (sw, Op[5], not_2_out, Op[3], not_4_out, Op[1], Op[0]);
  and and_5 (beq, not_1_out, not_2_out, not_3_out, Op[2], not_6_out, not_5_out);
  and and_6 (lui, not_1_out, not_2_out, Op[3], Op[2], Op[1], Op[0]);
  buf or_1 (RegDst, special);  // OR_Gate
  or or_2 (or_2_out[0], add, lw, sw);
  or or_3 (or_2_out[1], beq, sub);
  or or_4 (ALUSrc, ori, lw, sw, lui);
  BitFinder #(.width(16)) bitfinder_1 (
    .in({{11{1'b0}}, lui, sll, ori, or_2_out}), .index(bitfinder_1_index), .found(bitfinder_1_found));
  buf or_5 (MemtoReg, lw);  // OR_Gate
  Multiplexer #(.width(4)) multiplexer_1 (
    .in1(bitfinder_1_index), .out(ALUOp), .sel(bitfinder_1_found));  // open: in0, en
  or or_6 (RegWrite, special, ori, lw, lui);
  buf or_7 (MemRead, lw);  // OR_Gate
  buf or_8 (MemWrite, sw);  // OR_Gate
  buf or_9 (Branch, beq);  // OR_Gate
  or or_10 (ExtOp, lw, sw);
  not not_7 (not_7_out, Func[5]);
  not not_8 (not_8_out, Func[4]);
  not not_9 (not_9_out, Func[3]);
  not not_10 (not_10_out, Func[2]);
  not not_11 (not_11_out, Func[1]);
  not not_12 (not_12_out, Func[0]);
  and and_7 (add, Func[5], not_8_out, not_9_out, special, not_10_out, not_11_out, not_12_out);
  and and_8 (sub, Func[5], not_8_out, not_9_out, special, not_10_out, Func[1], not_12_out);
  and and_9 (sll, not_7_out, not_8_out, not_9_out, special, not_10_out, not_11_out, not_12_out);

  // Notes on the sheet:
  //   0 for add
  //   1 for sub
  //   2 for or
  //   3 for sll
  //   4 for lui
  //   5 for xor
endmodule

module DM_32bit (
  input  clk,
  input  RE,
  input  WE,
  input  rst,
  input  [31:0] DataAddr,
  input  [31:0] WriteData,
  output [31:0] Out
);

  RAM #(.addrWidth(12), .dataWidth(32), .bus("separate")) ram_1 (
    .addr(DataAddr[13:2]), .din(WriteData), .data(Out), .str(WE), .sel(1'b1), .clk(clk), .ld(RE), .clr(rst));
endmodule

module Ext (
  input  ExtOp,
  input  [15:0] In,
  output [31:0] Out
);

  wire [31:0] bit_extender_1_out, bit_extender_2_out;

  assign bit_extender_1_out = {{16{1'b0}}, In};  // Bit_Extender bit_extender_1
  assign bit_extender_2_out = {{16{In[15]}}, In};  // Bit_Extender bit_extender_2
  Multiplexer #(.width(32)) multiplexer_1 (
    .in0(bit_extender_1_out), .in1(bit_extender_2_out), .out(Out), .sel(ExtOp));  // open: en
endmodule

module Splitter (
  input  [31:0] Ins,
  output [5:0] Opcode,
  output [4:0] rs,
  output [4:0] rt,
  output [4:0] rd,
  output [4:0] s,
  output [5:0] Func,
  output [15:0] Imm,
  output [25:0] InsAddr
);


  assign Func = Ins[5:0];
  assign Imm = Ins[15:0];
  assign InsAddr = Ins[25:0];
  assign Opcode = Ins[31:26];
  assign rd = Ins[15:11];
  assign rs = Ins[25:21];
  assign rt = Ins[20:16];
  assign s = Ins[10:6];

  // Other names for the same wires on the sheet: _31_26[5:0] = Ins[31:26]; _5_0[5:0] = Ins[5:0];
  //   _10_6[4:0] = Ins[10:6]; _15_11[4:0] = Ins[15:11]; _20_16[4:0] = Ins[20:16]; _25_21[4:0] = Ins[25:21]
endmodule
